// Digital circuit BRANCH.dig as structural Verilog
module BRANCH (
  input  [2:0] fct3,
  input  [31:0] res,
  output Taken
);

  wire and_1_out, and_2_out, and_3_out, and_4_out, decoder_1_out_0, decoder_1_out_1, decoder_1_out_4,
       decoder_1_out_5, not_1_out, not_2_out, or_1_out, or_2_out, or_3_out, or_4_out, or_5_out, or_6_out,
       or_7_out, or_8_out, or_9_out, or_10_out;

  or or_1 (or_1_out, res[0], res[1], res[2], res[3], res[4]);
  or or_2 (or_2_out, res[5], res[6], res[7], res[8], res[9]);
  or or_3 (or_3_out, res[10], res[11], res[12], res[13], res[14]);
  or or_4 (or_4_out, res[15], res[16], res[17], res[18], res[19]);
  or or_5 (or_5_out, res[20], res[21], res[22], res[23], res[24]);
  or or_6 (or_6_out, res[25], res[26], res[27], res[28], res[29]);
  or or_7 (or_7_out, res[30], res[31]);
  or or_8 (or_8_out, or_1_out, or_2_out, or_3_out, or_4_out, or_5_out);
  or or_9 (or_9_out, or_6_out, or_7_out);
  or or_10 (or_10_out, or_8_out, or_9_out);
  Decoder #(.Selector_Bits(3)) decoder_1 (
    .sel(fct3), .out_0(decoder_1_out_0), .out_1(decoder_1_out_1), .out_4(decoder_1_out_4),
    .out_5(decoder_1_out_5));  // open: out_2, out_3, out_6, out_7
  not not_1 (not_1_out, or_10_out);
  not not_2 (not_2_out, res[31]);
  and and_1 (and_1_out, decoder_1_out_0, not_1_out);
  and and_2 (and_2_out, decoder_1_out_1, or_10_out);
  and and_3 (and_3_out, res[31], decoder_1_out_4);
  and and_4 (and_4_out, decoder_1_out_5, not_2_out);
  or or_11 (Taken, and_1_out, and_2_out, and_3_out, and_4_out);
endmodule
