// Digital circuit CB_EX.dig as structural Verilog
module CB_EX (
  input  [6:0] OP_CODE,
  output MUX_ALU,
  output MUX_FC3,
  output [1:0] MUX_SUB
);

  wire and_3_out, and_4_out, not_1_out, not_2_out, not_3_out, not_4_out, not_5_out, not_6_out, not_7_out,
       not_8_out, or_1_out, or_2_out, or_3_out;

  not not_1 (not_1_out, OP_CODE[3]);
  not not_2 (not_2_out, OP_CODE[4]);
  not not_3 (not_3_out, OP_CODE[5]);
  not not_4 (not_4_out, OP_CODE[6]);
  or or_1 (or_1_out, not_2_out, not_3_out);
  or or_2 (or_2_out, OP_CODE[5], not_4_out);
  not not_5 (not_5_out, OP_CODE[3]);
  not not_6 (not_6_out, OP_CODE[2]);
  and and_1 (MUX_SUB[0], not_4_out, OP_CODE[5], OP_CODE[4], not_5_out, not_6_out);
  and and_2 (MUX_SUB[1], OP_CODE[6], OP_CODE[5], not_2_out, not_1_out, not_6_out);
  not not_7 (not_7_out, OP_CODE[2]);
  not not_8 (not_8_out, OP_CODE[6]);
  and and_3 (and_3_out, OP_CODE[2], not_2_out, OP_CODE[5], OP_CODE[6]);
  and and_4 (and_4_out, not_7_out, not_8_out, or_1_out);
  and and_5 (MUX_FC3, not_2_out, not_1_out, not_7_out, or_2_out);
  or or_3 (or_3_out, and_3_out, and_4_out);
  and and_6 (MUX_ALU, or_3_out, not_1_out);
endmodule
