// Digital circuit EX_REG.dig as structural Verilog
module EX_REG (
  input  [31:0] RES,
  input  [31:0] PC_plus_4,
  input  W_EX,
  input  [31:0] SRC2,
  input  TAKEN,
  input  [4:0] RD,
  input  [6:0] OP_CODE,
  input  [31:0] IM,
  output [31:0] EX_PC_plus_4,
  output [31:0] EX_RES,
  output [31:0] EX_SRC2,
  output EX_TAKEN,
  output [4:0] EX_RD,
  output [6:0] EX_OP_CODE,
  output [31:0] EX_IM
);

  D_FF u_TAKEN (.D(TAKEN), .C(W_EX), .Q(EX_TAKEN));  // open: nQ
  D_FF #(.Bits(5)) u_RD (.D(RD), .C(W_EX), .Q(EX_RD));  // open: nQ
  D_FF #(.Bits(32)) SRC3 (.D(IM), .C(W_EX), .Q(EX_IM));  // open: nQ
  D_FF #(.Bits(7)) u_OP_CODE (.D(OP_CODE), .C(W_EX), .Q(EX_OP_CODE));  // open: nQ
  D_FF #(.Bits(32)) u_PC_plus_4 (.D(PC_plus_4), .C(W_EX), .Q(EX_PC_plus_4));  // open: nQ
  D_FF #(.Bits(32)) u_RES (.D(RES), .C(W_EX), .Q(EX_RES));  // open: nQ
  D_FF #(.Bits(32)) u_SRC2 (.D(SRC2), .C(W_EX), .Q(EX_SRC2));  // open: nQ
endmodule
