// Digital circuit MEM_REG.dig as structural Verilog
module MEM_REG (
  input  [31:0] RES,
  input  [31:0] PC_plus_4,
  input  W_MEM,
  input  TAKEN,
  input  [4:0] RD,
  input  [6:0] OP_CODE,
  input  [31:0] IM,
  output [31:0] MEM_PC_plus_4,
  output [31:0] MEM_RES,
  output MEM_TAKEN,
  output [4:0] MEM_RD,
  output [6:0] MEM_OP_CODE,
  output [31:0] MEM_IM
);

  D_FF #(.Bits(32)) u_RES (.D(RES), .C(W_MEM), .Q(MEM_RES));  // open: nQ
  D_FF u_TAKEN (.D(TAKEN), .C(W_MEM), .Q(MEM_TAKEN));  // open: nQ
  D_FF #(.Bits(5)) u_RD (.D(RD), .C(W_MEM), .Q(MEM_RD));  // open: nQ
  D_FF #(.Bits(32)) SRC3 (.D(IM), .C(W_MEM), .Q(MEM_IM));  // open: nQ
  D_FF #(.Bits(7)) u_OP_CODE (.D(OP_CODE), .C(W_MEM), .Q(MEM_OP_CODE));  // open: nQ
  D_FF #(.Bits(32)) u_PC_plus_4 (.D(PC_plus_4), .C(W_MEM), .Q(MEM_PC_plus_4));  // open: nQ
endmodule
