// Digital circuit DEC 2 4.dig as structural Verilog
module DEC_2_4 (
  input  e1,
  input  e0,
  output s0,
  output s1,
  output s2,
  output s3
);

  wire not_1_out, not_2_out, not_3_out, not_4_out;

  not not_1 (not_1_out, e1);
  not not_2 (not_2_out, e0);
  not not_3 (not_3_out, e1);
  not not_4 (not_4_out, e0);
  and and_1 (s0, not_1_out, not_2_out);
  and and_2 (s1, not_3_out, e0);
  and and_3 (s2, e1, not_4_out);
  and and_4 (s3, e1, e0);
endmodule
