// Digital circuit DEC 3 8.dig as structural Verilog
module DEC_3_8 (
  input  e2,
  input  e1,
  input  e0,
  output s0,
  output s1,
  output s2,
  output s3,
  output s4,
  output s5,
  output s6,
  output s7
);

  wire and_1_out, and_2_out, and_3_out, and_4_out, not_1_out, not_2_out, not_3_out;

  not not_1 (not_1_out, e1);
  not not_2 (not_2_out, e2);
  and and_1 (and_1_out, not_1_out, not_2_out);
  and and_2 (and_2_out, not_2_out, e1);
  and and_3 (and_3_out, e2, not_1_out);
  and and_4 (and_4_out, e2, e1);
  not not_3 (not_3_out, e0);
  and and_5 (s0, and_1_out, not_3_out);
  and and_6 (s1, and_1_out, e0);
  and and_7 (s2, and_2_out, not_3_out);
  and and_8 (s3, and_2_out, e0);
  and and_9 (s4, and_3_out, not_3_out);
  and and_10 (s5, and_3_out, e0);
  and and_11 (s6, and_4_out, not_3_out);
  and and_12 (s7, and_4_out, e0);
endmodule
