// Digital circuit MUX 8_1 Non_Rec.dig as structural Verilog
module MUX_8_1_Non_Rec (
  input  c0,
  input  c1,
  input  c2,
  input  e0,
  input  e1,
  input  e2,
  input  e3,
  input  e4,
  input  e5,
  input  e6,
  input  e7,
  output s
);

  wire and_1_out, and_2_out, and_3_out, and_4_out, and_5_out, and_6_out, and_7_out, and_8_out, and_9_out,
       and_10_out, and_11_out, and_12_out, and_13_out, and_14_out, and_15_out, and_16_out, and_17_out,
       and_18_out, and_19_out, and_20_out, and_21_out, and_22_out, and_23_out, and_24_out, not_1_out,
       not_2_out, not_3_out, or_1_out, or_2_out, or_3_out, or_4_out, or_5_out, or_6_out;

  not not_1 (not_1_out, c2);
  not not_2 (not_2_out, c1);
  not not_3 (not_3_out, c0);
  and and_1 (and_1_out, not_1_out, e0);
  and and_2 (and_2_out, not_1_out, e1);
  and and_3 (and_3_out, not_1_out, e2);
  and and_4 (and_4_out, not_1_out, e3);
  and and_5 (and_5_out, c2, e4);
  and and_6 (and_6_out, c2, e5);
  and and_7 (and_7_out, c2, e6);
  and and_8 (and_8_out, c2, e7);
  and and_9 (and_9_out, not_2_out, and_1_out);
  and and_10 (and_10_out, not_2_out, and_2_out);
  and and_11 (and_11_out, c1, and_3_out);
  and and_12 (and_12_out, c1, and_4_out);
  and and_13 (and_13_out, not_2_out, and_5_out);
  and and_14 (and_14_out, not_2_out, and_6_out);
  and and_15 (and_15_out, c1, and_7_out);
  and and_16 (and_16_out, c1, and_8_out);
  and and_17 (and_17_out, not_3_out, and_9_out);
  and and_18 (and_18_out, c0, and_10_out);
  and and_19 (and_19_out, not_3_out, and_11_out);
  and and_20 (and_20_out, c0, and_12_out);
  and and_21 (and_21_out, not_3_out, and_13_out);
  and and_22 (and_22_out, c0, and_14_out);
  and and_23 (and_23_out, not_3_out, and_15_out);
  and and_24 (and_24_out, c0, and_16_out);
  or or_1 (or_1_out, and_17_out, and_18_out);
  or or_2 (or_2_out, and_19_out, and_20_out);
  or or_3 (or_3_out, and_21_out, and_22_out);
  or or_4 (or_4_out, and_23_out, and_24_out);
  or or_5 (or_5_out, or_1_out, or_2_out);
  or or_6 (or_6_out, or_3_out, or_4_out);
  or or_7 (s, or_5_out, or_6_out);
endmodule
