// Digital circuit CC 1bit.dig as structural Verilog
module CC_1bit (
  input  G,
  input  P,
  input  Cin,
  output Cout
);

  wire and_1_out;

  and and_1 (and_1_out, P, Cin);
  or or_1 (Cout, G, and_1_out);

  // Notes on the sheet:
  //   Cin: Cin
endmodule
