// Digital circuit Compteur.dig as structural Verilog
module Compteur (
  input  clk,
  output s0,
  output s1,
  output s2
);

  wire and_1_out, and_2_out, and_3_out, D0_nq, D2_nq, not_1_out, or_1_out, xor_1_out;

  or or_1 (or_1_out, and_2_out, and_1_out);
  and and_1 (and_1_out, s2, not_1_out);
  not not_1 (not_1_out, and_3_out);
  and and_2 (and_2_out, D2_nq, and_3_out);
  D_FF D2 (.D(or_1_out), .C(clk), .Q(s2), .nQ(D2_nq));
  and and_3 (and_3_out, s1, s0);
  xor xor_1 (xor_1_out, s1, s0);
  D_FF D1 (.D(xor_1_out), .C(clk), .Q(s1));  // open: nQ
  D_FF D0 (.D(D0_nq), .C(clk), .Q(s0), .nQ(D0_nq));
endmodule
