// Digital circuit Compteur_Decompteur.dig as structural Verilog
module Compteur_Decompteur (
  input  W,
  input  inc,
  output s0,
  output s1,
  output s2
);

  wire and_1_out, and_2_out, and_3_out, and_4_out, D0_nq, D2_nq, multiplexer_1_out, multiplexer_2_out,
       not_1_out, not_2_out, not_3_out, or_1_out, or_2_out, or_3_out, or_4_out, xor_1_out;

  or or_1 (or_1_out, and_1_out, not_1_out);
  or or_2 (or_2_out, and_3_out, and_2_out);
  not not_1 (not_1_out, or_3_out);
  Multiplexer multiplexer_1 (.sel(inc), .in_0(or_1_out), .in_1(or_2_out), .out(multiplexer_1_out));
  or or_3 (or_3_out, or_4_out, s2);
  and and_1 (and_1_out, s2, or_4_out);
  not not_2 (not_2_out, and_4_out);
  and and_2 (and_2_out, s2, not_2_out);
  D_FF D2 (.D(multiplexer_1_out), .C(W), .Q(s2), .nQ(D2_nq));
  and and_3 (and_3_out, D2_nq, and_4_out);
  or or_4 (or_4_out, s0, s1);
  and and_4 (and_4_out, s1, s0);
  xor xor_1 (xor_1_out, s1, s0);
  not not_3 (not_3_out, xor_1_out);
  Multiplexer multiplexer_2 (.sel(inc), .in_0(not_3_out), .in_1(xor_1_out), .out(multiplexer_2_out));
  D_FF D1 (.D(multiplexer_2_out), .C(W), .Q(s1));  // open: nQ
  D_FF D0 (.D(D0_nq), .C(W), .Q(s0), .nQ(D0_nq));
endmodule
