// Digital circuit Compteur_4bit.dig as structural Verilog
module Compteur_4bit (
  input  clk,
  output s0,
  output s1
);

  wire D0_nq, xor_1_out;

  xor xor_1 (xor_1_out, s1, s0);
  D_FF D1 (.D(xor_1_out), .C(clk), .Q(s1));  // open: nQ
  D_FF D0 (.D(D0_nq), .C(clk), .Q(s0), .nQ(D0_nq));
endmodule
