// Digital circuit Registre_8Bit.dig as structural Verilog
module Registre_8Bit (
  input  e7,
  input  e6,
  input  e5,
  input  e4,
  input  e3,
  input  e2,
  input  e1,
  input  e0,
  input  W,
  input  reset,
  output s7,
  output s6,
  output s5,
  output s4,
  output s3,
  output s2,
  output s1,
  output s0
);

  wire d_ff_1_q, d_ff_2_q, d_ff_3_q, d_ff_4_q, d_ff_5_q, d_ff_6_q, d_ff_7_q, d_ff_8_q, not_1_out;

  not not_1 (not_1_out, reset);
  D_FF d_ff_1 (.D(e7), .C(W), .Q(d_ff_1_q));  // open: nQ
  and and_1 (s7, not_1_out, d_ff_1_q);
  D_FF d_ff_2 (.D(e6), .C(W), .Q(d_ff_2_q));  // open: nQ
  and and_2 (s6, not_1_out, d_ff_2_q);
  D_FF d_ff_3 (.D(e5), .C(W), .Q(d_ff_3_q));  // open: nQ
  and and_3 (s5, not_1_out, d_ff_3_q);
  D_FF d_ff_4 (.D(e4), .C(W), .Q(d_ff_4_q));  // open: nQ
  and and_4 (s4, not_1_out, d_ff_4_q);
  D_FF d_ff_5 (.D(e3), .C(W), .Q(d_ff_5_q));  // open: nQ
  and and_5 (s3, not_1_out, d_ff_5_q);
  D_FF d_ff_6 (.D(e2), .C(W), .Q(d_ff_6_q));  // open: nQ
  and and_6 (s2, not_1_out, d_ff_6_q);
  D_FF d_ff_7 (.D(e1), .C(W), .Q(d_ff_7_q));  // open: nQ
  and and_7 (s1, not_1_out, d_ff_7_q);
  D_FF d_ff_8 (.D(e0), .C(W), .Q(d_ff_8_q));  // open: nQ
  and and_8 (s0, not_1_out, d_ff_8_q);
endmodule
