// Digital circuit Registre_decalage_droite_gauche_4bit.dig as structural Verilog
module Registre_decalage_droite_gauche_4bit (
  input  W,
  input  left,
  input  dec,
  input  e3,
  input  e2,
  input  e1,
  input  e0,
  output s3,
  output s2,
  output s1,
  output s0
);

  wire multiplexer_1_out, multiplexer_2_out, multiplexer_3_out, multiplexer_4_out;

  Multiplexer #(.Selector_Bits(2)) multiplexer_1 (
    .sel({left, dec}), .in_0(e3), .in_1(1'b0), .in_2(e3), .in_3(s2), .out(multiplexer_1_out));
  D_FF d_ff_1 (.D(multiplexer_1_out), .C(W), .Q(s3));  // open: nQ
  Multiplexer #(.Selector_Bits(2)) multiplexer_2 (
    .sel({left, dec}), .in_0(e2), .in_1(s3), .in_2(e2), .in_3(s1), .out(multiplexer_2_out));
  D_FF d_ff_2 (.D(multiplexer_2_out), .C(W), .Q(s2));  // open: nQ
  Multiplexer #(.Selector_Bits(2)) multiplexer_3 (
    .sel({left, dec}), .in_0(e1), .in_1(s2), .in_2(e1), .in_3(s0), .out(multiplexer_3_out));
  D_FF d_ff_3 (.D(multiplexer_3_out), .C(W), .Q(s1));  // open: nQ
  Multiplexer #(.Selector_Bits(2)) multiplexer_4 (
    .sel({left, dec}), .in_0(e0), .in_1(s1), .in_2(e0), .in_3(1'b0), .out(multiplexer_4_out));
  D_FF d_ff_4 (.D(multiplexer_4_out), .C(W), .Q(s0));  // open: nQ
endmodule
