// Digital circuit Mux8Rec.dig as structural Verilog
module Mux8Rec (
  input  e0,
  input  e1,
  input  e2,
  input  e3,
  input  e4,
  input  e5,
  input  e6,
  input  e7,
  input  c2,
  input  c1,
  input  c0,
  output s
);

  wire and_1_out, and_2_out, and_3_out, and_4_out, and_5_out, and_6_out, and_7_out, and_8_out, and_9_out,
       and_10_out, and_11_out, and_12_out, and_13_out, and_14_out, not_1_out, not_2_out, not_3_out,
       not_4_out, not_5_out, not_6_out, or_1_out, or_2_out, or_3_out, or_4_out, or_5_out, or_6_out;

  not not_1 (not_1_out, c2);
  not not_2 (not_2_out, c2);
  not not_3 (not_3_out, c2);
  not not_4 (not_4_out, c2);
  and and_1 (and_1_out, e0, not_1_out);
  and and_2 (and_2_out, e1, c2);
  and and_3 (and_3_out, e2, not_2_out);
  and and_4 (and_4_out, e3, c2);
  and and_5 (and_5_out, e4, not_3_out);
  and and_6 (and_6_out, e5, c2);
  and and_7 (and_7_out, e6, not_4_out);
  and and_8 (and_8_out, e7, c2);
  or or_1 (or_1_out, and_1_out, and_2_out);
  or or_2 (or_2_out, and_3_out, and_4_out);
  or or_3 (or_3_out, and_5_out, and_6_out);
  or or_4 (or_4_out, and_7_out, and_8_out);
  not not_5 (not_5_out, c1);
  and and_9 (and_9_out, or_1_out, not_5_out);
  and and_10 (and_10_out, or_2_out, c1);
  and and_11 (and_11_out, or_3_out, not_5_out);
  and and_12 (and_12_out, or_4_out, c1);
  or or_5 (or_5_out, and_9_out, and_10_out);
  or or_6 (or_6_out, and_11_out, and_12_out);
  not not_6 (not_6_out, c0);
  and and_13 (and_13_out, or_5_out, not_6_out);
  and and_14 (and_14_out, or_6_out, c0);
  or or_7 (s, and_13_out, and_14_out);
endmodule
