// Digital circuit AddPG 1bit.dig as structural Verilog
module AddPG_1bit (
  input  a,
  input  b,
  input  Cin,
  output s,
  output G,
  output P
);

  wire xor_1_out;

  xor xor_1 (xor_1_out, a, b);
  xor xor_2 (s, xor_1_out, Cin);
  and and_1 (G, a, b);
  or or_1 (P, a, b);
endmodule
