// Digital circuit Or_8bit.dig as structural Verilog
module Or_8bit (
  input  a0,
  input  b0,
  input  a1,
  input  b1,
  input  a2,
  input  b2,
  input  a3,
  input  b3,
  input  a4,
  input  b4,
  input  a5,
  input  b5,
  input  a6,
  input  b6,
  input  a7,
  input  b7,
  output s0,
  output s1,
  output s2,
  output s3,
  output s4,
  output s5,
  output s6,
  output s7
);

  or or_1 (s0, a0, b0);
  or or_2 (s1, a1, b1);
  or or_3 (s2, a2, b2);
  or or_4 (s3, a3, b3);
  or or_5 (s4, a4, b4);
  or or_6 (s5, a5, b5);
  or or_7 (s6, a6, b6);
  or or_8 (s7, a7, b7);
endmodule
