// Digital circuit UAL.dig as structural Verilog
module UAL (
);

  add_sous8bit add_sous8bit_1 ();  // open: b0, a0, b1, a1, b2, a2, b3, a3, b4, a4, b5, a5, b6, a6, b7, a7, Cin, SUB, S7, Cout, S6, S5, S4, S3, S2, S1, S0
  Or_8bit or_8bit_1 ();  // open: a0, b0, a1, b1, a2, b2, a3, b3, a4, b4, a5, b5, a6, b6, a7, b7, s0, s1, s2, s3, s4, s5, s6, s7
  Xor_8bit xor_8bit_1 ();  // open: a0, b0, a1, b1, a2, b2, a3, b3, a4, b4, a5, b5, a6, b6, a7, b7, s0, s1, s2, s3, s4, s5, s6, s7
  And_8bit and_8bit_1 ();  // open: a0, b0, a1, b1, a2, b2, a3, b3, a4, b4, a5, b5, a6, b6, a7, b7, s0, s1, s2, s3, s4, s5, s6, s7
endmodule
