// Digital circuit add_sous8bit.dig as structural Verilog
module add_sous8bit (
  input  b0,
  input  a0,
  input  b1,
  input  a1,
  input  b2,
  input  a2,
  input  b3,
  input  a3,
  input  b4,
  input  a4,
  input  b5,
  input  a5,
  input  b6,
  input  a6,
  input  b7,
  input  a7,
  input  Cin,
  input  SUB,
  output S7,
  output Cout,
  output S6,
  output S5,
  output S4,
  output S3,
  output S2,
  output S1,
  output S0
);

  wire add_1bit_2_cout, add_1bit_3_cout, add_1bit_4_cout, add_1bit_5_cout, add_1bit_6_cout, add_1bit_7_cout,
       add_1bit_8_cout, xor_1_out, xor_2_out, xor_3_out, xor_4_out, xor_5_out, xor_6_out, xor_7_out,
       xor_8_out;

  xor xor_1 (xor_1_out, b7, SUB);
  Add_1bit add_1bit_1 (.a(a7), .b(xor_1_out), .cin(add_1bit_2_cout), .S(S7), .Cout(Cout));
  xor xor_2 (xor_2_out, b6, SUB);
  Add_1bit add_1bit_2 (.a(a6), .b(xor_2_out), .cin(add_1bit_3_cout), .S(S6), .Cout(add_1bit_2_cout));
  xor xor_3 (xor_3_out, b5, SUB);
  Add_1bit add_1bit_3 (.a(a5), .b(xor_3_out), .cin(add_1bit_4_cout), .S(S5), .Cout(add_1bit_3_cout));
  xor xor_4 (xor_4_out, b4, SUB);
  Add_1bit add_1bit_4 (.a(a4), .b(xor_4_out), .cin(add_1bit_5_cout), .S(S4), .Cout(add_1bit_4_cout));
  xor xor_5 (xor_5_out, b3, SUB);
  Add_1bit add_1bit_5 (.a(a3), .b(xor_5_out), .cin(add_1bit_6_cout), .S(S3), .Cout(add_1bit_5_cout));
  xor xor_6 (xor_6_out, b2, SUB);
  Add_1bit add_1bit_6 (.a(a2), .b(xor_6_out), .cin(add_1bit_7_cout), .S(S2), .Cout(add_1bit_6_cout));
  xor xor_7 (xor_7_out, b1, SUB);
  Add_1bit add_1bit_7 (.a(a1), .b(xor_7_out), .cin(add_1bit_8_cout), .S(S1), .Cout(add_1bit_7_cout));
  xor xor_8 (xor_8_out, b0, SUB);
  Add_1bit add_1bit_8 (.a(a0), .b(xor_8_out), .cin(Cin), .S(S0), .Cout(add_1bit_8_cout));
endmodule
