// Digital circuit Registre_decalage_droite_gauche_8bit.dig as structural Verilog
module Registre_decalage_droite_gauche_8bit (
  input  W,
  input  left,
  input  dec,
  input  e7,
  input  e6,
  input  e5,
  input  e4,
  input  e8,
  input  e9,
  input  e10,
  input  e11,
  output s7,
  output s6,
  output s5,
  output s4,
  output s3,
  output s2,
  output s1,
  output s0
);

  wire multiplexer_1_out, multiplexer_2_out, multiplexer_3_out, multiplexer_4_out, multiplexer_5_out,
       multiplexer_6_out, multiplexer_7_out, multiplexer_8_out;

  Multiplexer #(.Selector_Bits(2)) multiplexer_1 (
    .sel({left, dec}), .in_0(e7), .in_1(1'b0), .in_2(e7), .in_3(s6), .out(multiplexer_1_out));
  D_FF d_ff_1 (.D(multiplexer_1_out), .C(W), .Q(s7));  // open: nQ
  Multiplexer #(.Selector_Bits(2)) multiplexer_2 (
    .sel({left, dec}), .in_0(e6), .in_1(s7), .in_2(e6), .in_3(s5), .out(multiplexer_2_out));
  D_FF d_ff_2 (.D(multiplexer_2_out), .C(W), .Q(s6));  // open: nQ
  Multiplexer #(.Selector_Bits(2)) multiplexer_3 (
    .sel({left, dec}), .in_0(e5), .in_1(s6), .in_2(e5), .in_3(s4), .out(multiplexer_3_out));
  D_FF d_ff_3 (.D(multiplexer_3_out), .C(W), .Q(s5));  // open: nQ
  Multiplexer #(.Selector_Bits(2)) multiplexer_4 (
    .sel({left, dec}), .in_0(e4), .in_1(s5), .in_2(e4), .in_3(s3), .out(multiplexer_4_out));
  D_FF d_ff_4 (.D(multiplexer_4_out), .C(W), .Q(s4));  // open: nQ
  Multiplexer #(.Selector_Bits(2)) multiplexer_5 (
    .sel({left, dec}), .in_0(e8), .in_1(s4), .in_2(e8), .in_3(s2), .out(multiplexer_5_out));
  D_FF d_ff_5 (.D(multiplexer_5_out), .C(W), .Q(s3));  // open: nQ
  Multiplexer #(.Selector_Bits(2)) multiplexer_6 (
    .sel({left, dec}), .in_0(e9), .in_1(s3), .in_2(e9), .in_3(s1), .out(multiplexer_6_out));
  D_FF d_ff_6 (.D(multiplexer_6_out), .C(W), .Q(s2));  // open: nQ
  Multiplexer #(.Selector_Bits(2)) multiplexer_7 (
    .sel({left, dec}), .in_0(e10), .in_1(s2), .in_2(e10), .in_3(s0), .out(multiplexer_7_out));
  D_FF d_ff_7 (.D(multiplexer_7_out), .C(W), .Q(s1));  // open: nQ
  Multiplexer #(.Selector_Bits(2)) multiplexer_8 (
    .sel({left, dec}), .in_0(e11), .in_1(s1), .in_2(e11), .in_3(1'b0), .out(multiplexer_8_out));
  D_FF d_ff_8 (.D(multiplexer_8_out), .C(W), .Q(s0));  // open: nQ
endmodule
