// Digital circuit Compteur.dig as structural Verilog
module Compteur (
  input  W,
  output s7,
  output s6,
  output s5,
  output s4,
  output s3,
  output s2,
  output s1,
  output s0
);

  wire multiplexer_1_out, undriven;

  D_FF d_ff_1 (.C(W), .Q(s7));  // open: D, nQ
  D_FF d_ff_2 (.C(W), .Q(s6));  // open: D, nQ
  D_FF d_ff_3 (.C(W), .Q(s5));  // open: D, nQ
  D_FF d_ff_4 (.C(W), .Q(s4));  // open: D, nQ
  D_FF d_ff_5 (.C(W), .Q(s3));  // open: D, nQ
  D_FF d_ff_6 (.C(W), .Q(s2));  // open: D, nQ
  D_FF d_ff_7 (.C(W), .Q(s1));  // open: D, nQ
  Multiplexer multiplexer_1 (.in_0(undriven), .out(multiplexer_1_out));  // open: sel, in_1
  D_FF d_ff_8 (.D(multiplexer_1_out), .C(W), .Q(s0));  // open: nQ
endmodule
