// Digital circuit Banc_De_Registres.dig as structural Verilog
module Banc_De_Registres (
  input  Wreg,
  input  [4:0] rd,
  input  [4:0] rs1,
  input  [4:0] rs2,
  input  [31:0] res,
  output [31:0] src1,
  output [31:0] src2,
  output [31:0] x3,
  output [31:0] x5,
  output [31:0] x6,
  output [31:0] x7,
  output [31:0] x10
);

  wire and_1_out, and_2_out, and_3_out, and_4_out, and_5_out, and_6_out, and_7_out, and_8_out, and_9_out,
       and_10_out, and_11_out, and_12_out, and_13_out, and_14_out, and_15_out, and_16_out, and_17_out,
       and_18_out, and_19_out, and_20_out, and_21_out, and_22_out, and_23_out, and_24_out, and_25_out,
       and_26_out, and_27_out, and_28_out, and_29_out, and_30_out, and_31_out, decoder_1_out_0,
       decoder_1_out_1, decoder_1_out_2, decoder_1_out_3, decoder_1_out_4, decoder_1_out_5, decoder_1_out_6,
       decoder_1_out_7, decoder_1_out_8, decoder_1_out_9, decoder_1_out_10, decoder_1_out_11,
       decoder_1_out_12, decoder_1_out_13, decoder_1_out_14, decoder_1_out_15, decoder_1_out_16,
       decoder_1_out_17, decoder_1_out_18, decoder_1_out_19, decoder_1_out_20, decoder_1_out_21,
       decoder_1_out_22, decoder_1_out_23, decoder_1_out_24, decoder_1_out_25, decoder_1_out_26,
       decoder_1_out_27, decoder_1_out_28, decoder_1_out_29, decoder_1_out_30, decoder_1_out_31,
       decoder_2_out_0, decoder_2_out_1, decoder_2_out_2, decoder_2_out_3, decoder_2_out_4, decoder_2_out_5,
       decoder_2_out_6, decoder_2_out_7, decoder_2_out_8, decoder_2_out_9, decoder_2_out_10,
       decoder_2_out_11, decoder_2_out_12, decoder_2_out_13, decoder_2_out_14, decoder_2_out_15,
       decoder_2_out_16, decoder_2_out_17, decoder_2_out_18, decoder_2_out_19, decoder_2_out_20,
       decoder_2_out_21, decoder_2_out_22, decoder_2_out_23, decoder_2_out_24, decoder_2_out_25,
       decoder_2_out_26, decoder_2_out_27, decoder_2_out_28, decoder_2_out_29, decoder_2_out_30,
       decoder_2_out_31, decoder_3_out_0, decoder_3_out_1, decoder_3_out_2, decoder_3_out_3, decoder_3_out_4,
       decoder_3_out_5, decoder_3_out_6, decoder_3_out_7, decoder_3_out_8, decoder_3_out_9, decoder_3_out_10,
       decoder_3_out_11, decoder_3_out_12, decoder_3_out_13, decoder_3_out_14, decoder_3_out_15,
       decoder_3_out_16, decoder_3_out_17, decoder_3_out_18, decoder_3_out_19, decoder_3_out_20,
       decoder_3_out_21, decoder_3_out_22, decoder_3_out_23, decoder_3_out_24, decoder_3_out_25,
       decoder_3_out_26, decoder_3_out_27, decoder_3_out_28, decoder_3_out_29, decoder_3_out_30,
       decoder_3_out_31;
  wire [31:0] r1_q, r2_q, r4_q, r8_q, r9_q, r11_q, r12_q, r13_q, r14_q, r15_q, r16_q, r17_q, r18_q, r19_q,
       r20_q, r21_q, r22_q, r23_q, r24_q, r25_q, r26_q, r27_q, r28_q, r29_q, r30_q, r31_q;

  Decoder #(.Selector_Bits(5)) decoder_1 (
    .sel(rd), .out_0(decoder_1_out_0), .out_1(decoder_1_out_1), .out_2(decoder_1_out_2),
    .out_3(decoder_1_out_3), .out_4(decoder_1_out_4), .out_5(decoder_1_out_5), .out_6(decoder_1_out_6),
    .out_7(decoder_1_out_7), .out_8(decoder_1_out_8), .out_9(decoder_1_out_9), .out_10(decoder_1_out_10),
    .out_11(decoder_1_out_11), .out_12(decoder_1_out_12), .out_13(decoder_1_out_13),
    .out_14(decoder_1_out_14), .out_15(decoder_1_out_15), .out_16(decoder_1_out_16),
    .out_17(decoder_1_out_17), .out_18(decoder_1_out_18), .out_19(decoder_1_out_19),
    .out_20(decoder_1_out_20), .out_21(decoder_1_out_21), .out_22(decoder_1_out_22),
    .out_23(decoder_1_out_23), .out_24(decoder_1_out_24), .out_25(decoder_1_out_25),
    .out_26(decoder_1_out_26), .out_27(decoder_1_out_27), .out_28(decoder_1_out_28),
    .out_29(decoder_1_out_29), .out_30(decoder_1_out_30), .out_31(decoder_1_out_31));
  and and_1 (and_1_out, decoder_1_out_1, Wreg);
  and and_2 (and_2_out, decoder_1_out_2, Wreg);
  and and_3 (and_3_out, decoder_1_out_3, Wreg);
  and and_4 (and_4_out, decoder_1_out_4, Wreg);
  and and_5 (and_5_out, decoder_1_out_5, Wreg);
  and and_6 (and_6_out, decoder_1_out_6, Wreg);
  and and_7 (and_7_out, decoder_1_out_7, Wreg);
  and and_8 (and_8_out, decoder_1_out_8, Wreg);
  and and_9 (and_9_out, decoder_1_out_9, Wreg);
  and and_10 (and_10_out, decoder_1_out_10, Wreg);
  and and_11 (and_11_out, decoder_1_out_11, Wreg);
  and and_12 (and_12_out, decoder_1_out_12, Wreg);
  and and_13 (and_13_out, decoder_1_out_13, Wreg);
  and and_14 (and_14_out, decoder_1_out_14, Wreg);
  and and_15 (and_15_out, decoder_1_out_15, Wreg);
  and and_16 (and_16_out, decoder_1_out_16, Wreg);
  and and_17 (and_17_out, decoder_1_out_17, Wreg);
  and and_18 (and_18_out, decoder_1_out_18, Wreg);
  and and_19 (and_19_out, decoder_1_out_19, Wreg);
  and and_20 (and_20_out, decoder_1_out_20, Wreg);
  and and_21 (and_21_out, decoder_1_out_21, Wreg);
  and and_22 (and_22_out, decoder_1_out_22, Wreg);
  and and_23 (and_23_out, decoder_1_out_23, Wreg);
  and and_24 (and_24_out, decoder_1_out_24, Wreg);
  and and_25 (and_25_out, decoder_1_out_25, Wreg);
  and and_26 (and_26_out, decoder_1_out_26, Wreg);
  and and_27 (and_27_out, decoder_1_out_27, Wreg);
  and and_28 (and_28_out, decoder_1_out_28, Wreg);
  and and_29 (and_29_out, decoder_1_out_29, Wreg);
  and and_30 (and_30_out, decoder_1_out_30, Wreg);
  and and_31 (and_31_out, decoder_1_out_31, Wreg);
  D_FF #(.Bits(32)) r1 (.D(res), .C(and_1_out), .Q(r1_q));  // open: nQ
  D_FF #(.Bits(32)) r2 (.D(res), .C(and_2_out), .Q(r2_q));  // open: nQ
  D_FF #(.Bits(32)) r3 (.D(res), .C(and_3_out), .Q(x3));  // open: nQ
  D_FF #(.Bits(32)) r4 (.D(res), .C(and_4_out), .Q(r4_q));  // open: nQ
  D_FF #(.Bits(32)) r5 (.D(res), .C(and_5_out), .Q(x5));  // open: nQ
  D_FF #(.Bits(32)) r6 (.D(res), .C(and_6_out), .Q(x6));  // open: nQ
  D_FF #(.Bits(32)) r7 (.D(res), .C(and_7_out), .Q(x7));  // open: nQ
  D_FF #(.Bits(32)) r8 (.D(res), .C(and_8_out), .Q(r8_q));  // open: nQ
  D_FF #(.Bits(32)) r9 (.D(res), .C(and_9_out), .Q(r9_q));  // open: nQ
  D_FF #(.Bits(32)) r10 (.D(res), .C(and_10_out), .Q(x10));  // open: nQ
  D_FF #(.Bits(32)) r11 (.D(res), .C(and_11_out), .Q(r11_q));  // open: nQ
  D_FF #(.Bits(32)) r12 (.D(res), .C(and_12_out), .Q(r12_q));  // open: nQ
  D_FF #(.Bits(32)) r13 (.D(res), .C(and_13_out), .Q(r13_q));  // open: nQ
  D_FF #(.Bits(32)) r14 (.D(res), .C(and_14_out), .Q(r14_q));  // open: nQ
  D_FF #(.Bits(32)) r15 (.D(res), .C(and_15_out), .Q(r15_q));  // open: nQ
  D_FF #(.Bits(32)) r16 (.D(res), .C(and_16_out), .Q(r16_q));  // open: nQ
  D_FF #(.Bits(32)) r17 (.D(res), .C(and_17_out), .Q(r17_q));  // open: nQ
  D_FF #(.Bits(32)) r18 (.D(res), .C(and_18_out), .Q(r18_q));  // open: nQ
  D_FF #(.Bits(32)) r19 (.D(res), .C(and_19_out), .Q(r19_q));  // open: nQ
  D_FF #(.Bits(32)) r20 (.D(res), .C(and_20_out), .Q(r20_q));  // open: nQ
  D_FF #(.Bits(32)) r21 (.D(res), .C(and_21_out), .Q(r21_q));  // open: nQ
  D_FF #(.Bits(32)) r22 (.D(res), .C(and_22_out), .Q(r22_q));  // open: nQ
  D_FF #(.Bits(32)) r23 (.D(res), .C(and_23_out), .Q(r23_q));  // open: nQ
  D_FF #(.Bits(32)) r24 (.D(res), .C(and_24_out), .Q(r24_q));  // open: nQ
  D_FF #(.Bits(32)) r25 (.D(res), .C(and_25_out), .Q(r25_q));  // open: nQ
  D_FF #(.Bits(32)) r26 (.D(res), .C(and_26_out), .Q(r26_q));  // open: nQ
  D_FF #(.Bits(32)) r27 (.D(res), .C(and_27_out), .Q(r27_q));  // open: nQ
  D_FF #(.Bits(32)) r28 (.D(res), .C(and_28_out), .Q(r28_q));  // open: nQ
  D_FF #(.Bits(32)) r29 (.D(res), .C(and_29_out), .Q(r29_q));  // open: nQ
  D_FF #(.Bits(32)) r30 (.D(res), .C(and_30_out), .Q(r30_q));  // open: nQ
  D_FF #(.Bits(32)) r31 (.D(res), .C(and_31_out), .Q(r31_q));  // open: nQ
  Decoder #(.Selector_Bits(5)) decoder_2 (
    .sel(rs1), .out_0(decoder_2_out_0), .out_1(decoder_2_out_1), .out_2(decoder_2_out_2),
    .out_3(decoder_2_out_3), .out_4(decoder_2_out_4), .out_5(decoder_2_out_5), .out_6(decoder_2_out_6),
    .out_7(decoder_2_out_7), .out_8(decoder_2_out_8), .out_9(decoder_2_out_9), .out_10(decoder_2_out_10),
    .out_11(decoder_2_out_11), .out_12(decoder_2_out_12), .out_13(decoder_2_out_13),
    .out_14(decoder_2_out_14), .out_15(decoder_2_out_15), .out_16(decoder_2_out_16),
    .out_17(decoder_2_out_17), .out_18(decoder_2_out_18), .out_19(decoder_2_out_19),
    .out_20(decoder_2_out_20), .out_21(decoder_2_out_21), .out_22(decoder_2_out_22),
    .out_23(decoder_2_out_23), .out_24(decoder_2_out_24), .out_25(decoder_2_out_25),
    .out_26(decoder_2_out_26), .out_27(decoder_2_out_27), .out_28(decoder_2_out_28),
    .out_29(decoder_2_out_29), .out_30(decoder_2_out_30), .out_31(decoder_2_out_31));
  assign src1 = decoder_2_out_0 ? {32{1'b0}} : 32'bz;  // Driver driver_1
  assign src1 = decoder_2_out_1 ? r1_q : 32'bz;  // Driver driver_2
  assign src1 = decoder_2_out_2 ? r2_q : 32'bz;  // Driver driver_3
  assign src1 = decoder_2_out_3 ? x3 : 32'bz;  // Driver driver_4
  assign src1 = decoder_2_out_4 ? r4_q : 32'bz;  // Driver driver_5
  assign src1 = decoder_2_out_5 ? x5 : 32'bz;  // Driver driver_6
  assign src1 = decoder_2_out_6 ? x6 : 32'bz;  // Driver driver_7
  assign src1 = decoder_2_out_7 ? x7 : 32'bz;  // Driver driver_8
  assign src1 = decoder_2_out_8 ? r8_q : 32'bz;  // Driver driver_9
  assign src1 = decoder_2_out_9 ? r9_q : 32'bz;  // Driver driver_10
  assign src1 = decoder_2_out_10 ? x10 : 32'bz;  // Driver driver_11
  assign src1 = decoder_2_out_11 ? r11_q : 32'bz;  // Driver driver_12
  assign src1 = decoder_2_out_12 ? r12_q : 32'bz;  // Driver driver_13
  assign src1 = decoder_2_out_13 ? r13_q : 32'bz;  // Driver driver_14
  assign src1 = decoder_2_out_14 ? r14_q : 32'bz;  // Driver driver_15
  assign src1 = decoder_2_out_15 ? r15_q : 32'bz;  // Driver driver_16
  assign src1 = decoder_2_out_16 ? r16_q : 32'bz;  // Driver driver_17
  assign src1 = decoder_2_out_17 ? r17_q : 32'bz;  // Driver driver_18
  assign src1 = decoder_2_out_18 ? r18_q : 32'bz;  // Driver driver_19
  assign src1 = decoder_2_out_19 ? r19_q : 32'bz;  // Driver driver_20
  assign src1 = decoder_2_out_20 ? r20_q : 32'bz;  // Driver driver_21
  assign src1 = decoder_2_out_21 ? r21_q : 32'bz;  // Driver driver_22
  assign src1 = decoder_2_out_22 ? r22_q : 32'bz;  // Driver driver_23
  assign src1 = decoder_2_out_23 ? r23_q : 32'bz;  // Driver driver_24
  assign src1 = decoder_2_out_24 ? r24_q : 32'bz;  // Driver driver_25
  assign src1 = decoder_2_out_25 ? r25_q : 32'bz;  // Driver driver_26
  assign src1 = decoder_2_out_26 ? r26_q : 32'bz;  // Driver driver_27
  assign src1 = decoder_2_out_27 ? r27_q : 32'bz;  // Driver driver_28
  assign src1 = decoder_2_out_28 ? r28_q : 32'bz;  // Driver driver_29
  assign src1 = decoder_2_out_29 ? r29_q : 32'bz;  // Driver driver_30
  assign src1 = decoder_2_out_30 ? r30_q : 32'bz;  // Driver driver_31
  assign src1 = decoder_2_out_31 ? r31_q : 32'bz;  // Driver driver_32
  Decoder #(.Selector_Bits(5)) decoder_3 (
    .sel(rs2), .out_0(decoder_3_out_0), .out_1(decoder_3_out_1), .out_2(decoder_3_out_2),
    .out_3(decoder_3_out_3), .out_4(decoder_3_out_4), .out_5(decoder_3_out_5), .out_6(decoder_3_out_6),
    .out_7(decoder_3_out_7), .out_8(decoder_3_out_8), .out_9(decoder_3_out_9), .out_10(decoder_3_out_10),
    .out_11(decoder_3_out_11), .out_12(decoder_3_out_12), .out_13(decoder_3_out_13),
    .out_14(decoder_3_out_14), .out_15(decoder_3_out_15), .out_16(decoder_3_out_16),
    .out_17(decoder_3_out_17), .out_18(decoder_3_out_18), .out_19(decoder_3_out_19),
    .out_20(decoder_3_out_20), .out_21(decoder_3_out_21), .out_22(decoder_3_out_22),
    .out_23(decoder_3_out_23), .out_24(decoder_3_out_24), .out_25(decoder_3_out_25),
    .out_26(decoder_3_out_26), .out_27(decoder_3_out_27), .out_28(decoder_3_out_28),
    .out_29(decoder_3_out_29), .out_30(decoder_3_out_30), .out_31(decoder_3_out_31));
  assign src2 = decoder_3_out_0 ? {32{1'b0}} : 32'bz;  // Driver driver_33
  assign src2 = decoder_3_out_1 ? r1_q : 32'bz;  // Driver driver_34
  assign src2 = decoder_3_out_2 ? r2_q : 32'bz;  // Driver driver_35
  assign src2 = decoder_3_out_3 ? x3 : 32'bz;  // Driver driver_36
  assign src2 = decoder_3_out_4 ? r4_q : 32'bz;  // Driver driver_37
  assign src2 = decoder_3_out_5 ? x5 : 32'bz;  // Driver driver_38
  assign src2 = decoder_3_out_6 ? x6 : 32'bz;  // Driver driver_39
  assign src2 = decoder_3_out_7 ? x7 : 32'bz;  // Driver driver_40
  assign src2 = decoder_3_out_8 ? r8_q : 32'bz;  // Driver driver_41
  assign src2 = decoder_3_out_9 ? r9_q : 32'bz;  // Driver driver_42
  assign src2 = decoder_3_out_10 ? x10 : 32'bz;  // Driver driver_43
  assign src2 = decoder_3_out_11 ? r11_q : 32'bz;  // Driver driver_44
  assign src2 = decoder_3_out_12 ? r12_q : 32'bz;  // Driver driver_45
  assign src2 = decoder_3_out_13 ? r13_q : 32'bz;  // Driver driver_46
  assign src2 = decoder_3_out_14 ? r14_q : 32'bz;  // Driver driver_47
  assign src2 = decoder_3_out_15 ? r15_q : 32'bz;  // Driver driver_48
  assign src2 = decoder_3_out_16 ? r16_q : 32'bz;  // Driver driver_49
  assign src2 = decoder_3_out_17 ? r17_q : 32'bz;  // Driver driver_50
  assign src2 = decoder_3_out_18 ? r18_q : 32'bz;  // Driver driver_51
  assign src2 = decoder_3_out_19 ? r19_q : 32'bz;  // Driver driver_52
  assign src2 = decoder_3_out_20 ? r20_q : 32'bz;  // Driver driver_53
  assign src2 = decoder_3_out_21 ? r21_q : 32'bz;  // Driver driver_54
  assign src2 = decoder_3_out_22 ? r22_q : 32'bz;  // Driver driver_55
  assign src2 = decoder_3_out_23 ? r23_q : 32'bz;  // Driver driver_56
  assign src2 = decoder_3_out_24 ? r24_q : 32'bz;  // Driver driver_57
  assign src2 = decoder_3_out_25 ? r25_q : 32'bz;  // Driver driver_58
  assign src2 = decoder_3_out_26 ? r26_q : 32'bz;  // Driver driver_59
  assign src2 = decoder_3_out_27 ? r27_q : 32'bz;  // Driver driver_60
  assign src2 = decoder_3_out_28 ? r28_q : 32'bz;  // Driver driver_61
  assign src2 = decoder_3_out_29 ? r29_q : 32'bz;  // Driver driver_62
  assign src2 = decoder_3_out_30 ? r30_q : 32'bz;  // Driver driver_63
  assign src2 = decoder_3_out_31 ? r31_q : 32'bz;  // Driver driver_64
endmodule
