// Digital circuit CB_CALLBACK.dig as structural Verilog
module CB_CALLBACK (
  input  [6:0] OP_CODE,
  input  TAKEN,
  output MUX_JUMP,
  output MUX_RES,
  output MUX_PC,
  output MUX_JALR,
  output W_REG
);

  wire and_1_out, and_4_out, and_6_out, and_7_out, and_8_out, not_1_out, not_2_out, not_3_out, not_4_out,
       not_5_out, or_1_out, or_2_out;

  not not_1 (not_1_out, OP_CODE[2]);
  not not_2 (not_2_out, OP_CODE[3]);
  not not_3 (not_3_out, OP_CODE[4]);
  not not_4 (not_4_out, OP_CODE[5]);
  not not_5 (not_5_out, OP_CODE[6]);
  and and_1 (and_1_out, OP_CODE[3], OP_CODE[2]);
  or or_1 (or_1_out, not_4_out, OP_CODE[4]);
  and and_2 (MUX_JUMP, OP_CODE[2], not_2_out, not_3_out, OP_CODE[5], OP_CODE[6]);
  and and_3 (MUX_RES, OP_CODE[6], OP_CODE[5], not_3_out, OP_CODE[2]);
  and and_4 (and_4_out, not_1_out, not_2_out, TAKEN);
  and and_5 (MUX_JALR, OP_CODE[6], OP_CODE[5], not_3_out, not_2_out, OP_CODE[2]);
  and and_6 (and_6_out, OP_CODE[6], OP_CODE[5], not_3_out, OP_CODE[2]);
  and and_7 (and_7_out, not_3_out, OP_CODE[5], OP_CODE[6]);
  or or_2 (or_2_out, and_1_out, and_4_out);
  and and_8 (and_8_out, not_5_out, not_2_out, not_1_out, or_1_out);
  or or_3 (W_REG, and_6_out, and_8_out);
  and and_9 (MUX_PC, and_7_out, or_2_out);
endmodule
