// Digital circuit CB_MEM.dig as structural Verilog
module CB_MEM (
  input  [6:0] OP_CODE,
  output MUX_MEM,
  output W_MEM
);

  wire not_1_out, not_2_out, not_3_out, not_4_out, not_5_out;

  not not_1 (not_1_out, OP_CODE[2]);
  not not_2 (not_2_out, OP_CODE[3]);
  not not_3 (not_3_out, OP_CODE[4]);
  not not_4 (not_4_out, OP_CODE[5]);
  not not_5 (not_5_out, OP_CODE[6]);
  and and_1 (W_MEM, not_1_out, not_1_out, not_3_out, OP_CODE[5], not_5_out);
  and and_2 (MUX_MEM, not_1_out, not_2_out, not_3_out, not_4_out, not_5_out);
endmodule
