// Digital circuit C_MUX_IM.dig as structural Verilog
module C_MUX_IM (
  input  [6:0] OP_CODE,
  output [1:0] MUX_IMM
);

  wire and_1_out, and_2_out, not_1_out, not_2_out, not_3_out, not_4_out, not_5_out, or_1_out, xor_1_out;

  xor xor_1 (xor_1_out, OP_CODE[2], OP_CODE[3]);
  not not_1 (not_1_out, OP_CODE[2]);
  not not_2 (not_2_out, OP_CODE[3]);
  not not_3 (not_3_out, OP_CODE[6]);
  not not_4 (not_4_out, OP_CODE[4]);
  not not_5 (not_5_out, xor_1_out);
  and and_1 (and_1_out, OP_CODE[2], OP_CODE[3], OP_CODE[6]);
  and and_2 (and_2_out, not_1_out, not_2_out, not_3_out);
  or or_1 (or_1_out, and_1_out, and_2_out);
  and and_3 (MUX_IMM[0], not_4_out, OP_CODE[5], OP_CODE[6], not_5_out);
  and and_4 (MUX_IMM[1], or_1_out, not_4_out, OP_CODE[5]);
endmodule
