// Digital circuit Circuit_complet_2024.dig as structural Verilog
module Circuit_complet_2024 (
  input  W_BLOC
);

  wire branch_1_taken, cb_callback_1_mux_jalr, cb_callback_1_mux_jump, cb_callback_1_mux_pc,
       cb_callback_1_mux_res, cb_callback_1_w_reg, cb_ex_1_mux_alu, cb_ex_1_mux_fc3, cb_mem_1_mux_mem,
       cb_mem_1_w_mem, delay_1_out, multiplexer_6_out, not_1_out, not_2_out, undriven_14;
  wire [1:0] c_mux_im_1_mux_imm, cb_ex_1_mux_sub;
  wire [2:0] multiplexer_4_out, undriven_6;
  wire [4:0] undriven_2;
  wire [5:5] undriven_5;
  wire [6:0] undriven_4, undriven_10, undriven_13;
  wire [7:0] PC_q_2;
  wire [31:0] add_1_s, add_2_s, banc_de_registres_1_src1, banc_de_registres_1_src2, bitextender_1_out,
       bitextender_2_out, bitextender_3_out, bitextender_4_out, multiplexer_1_out, multiplexer_2_out,
       multiplexer_3_out, multiplexer_5_out, multiplexer_7_out, multiplexer_8_out, multiplexer_9_out, PC_q,
       ramsingleportsel_1_d, ramsingleportsel_2_d, ual_1_s, undriven, undriven_3, undriven_7, undriven_8,
       undriven_9, undriven_11, undriven_12, undriven_15, undriven_16;

  Multiplexer #(.Bits(32)) multiplexer_1 (
    .sel(cb_callback_1_mux_pc), .in_0(32'h4), .in_1(multiplexer_9_out), .out(multiplexer_1_out));
  Add #(.Bits(32)) add_1 (
    .a(multiplexer_1_out), .b({PC_q[31:10], PC_q_2, PC_q[1:0]}), .c_i(1'b0), .s(add_1_s));  // open: c_o
  Multiplexer #(.Bits(32)) multiplexer_2 (
    .sel(cb_callback_1_mux_jalr), .in_0(add_1_s), .in_1(multiplexer_9_out), .out(multiplexer_2_out));
  Delay delay_1 (.in(W_BLOC), .out(delay_1_out));
  D_FF #(.Bits(32)) PC (.D(multiplexer_2_out), .C(delay_1_out), .Q({PC_q[31:10], PC_q_2, PC_q[1:0]}));  // open: nQ
  RAMSinglePortSel #(.AddrBits(8), .Bits(32)) ramsingleportsel_1 (
    .A(PC_q_2), .CS(1'b1), .WE(not_1_out), .OE(1'b1), .D(ramsingleportsel_1_d));
  not not_1 (not_1_out, 1'b1);
  Add #(.Bits(32)) add_2 (.a({PC_q[31:10], PC_q_2, PC_q[1:0]}), .b(32'h4), .c_i(1'b0), .s(add_2_s));  // open: c_o
  IF_REG if_reg_1 ();
  BitExtender #(.inputBits(12), .outputBits(32)) bitextender_1 (.in(undriven[31:20]), .out(bitextender_1_out));
  BitExtender #(.inputBits(12), .outputBits(32)) bitextender_2 (
    .in({undriven[31:25], undriven[11:7]}), .out(bitextender_2_out));
  BitExtender #(.inputBits(14), .outputBits(32)) bitextender_3 (
    .in({undriven[31], undriven[7], undriven[30:25], undriven[11:8], 2'b00}), .out(bitextender_3_out));
  BitExtender #(.inputBits(22), .outputBits(32)) bitextender_4 (
    .in({undriven[31], undriven[19:12], undriven[20], undriven[30:21], 2'b00}), .out(bitextender_4_out));
  Banc_De_Registres banc_de_registres_1 (
    .Wreg(cb_callback_1_w_reg), .rd(undriven_2), .rs1(undriven[19:15]), .rs2(undriven[24:20]),
    .res(multiplexer_8_out), .src1(banc_de_registres_1_src1), .src2(banc_de_registres_1_src2));  // open: x3
  Multiplexer #(.Selector_Bits(2), .Bits(32)) multiplexer_3 (
    .sel(c_mux_im_1_mux_imm), .in_0(bitextender_1_out), .in_1(bitextender_2_out), .in_2(bitextender_3_out),
    .in_3(bitextender_4_out), .out(multiplexer_3_out));
  C_MUX_IM c_mux_im_1 (.OP_CODE(undriven[6:0]), .MUX_IMM(c_mux_im_1_mux_imm));
  ID_REG id_reg_1 ();
  CB_EX cb_ex_1 (.OP_CODE(undriven_4), .MUX_ALU(cb_ex_1_mux_alu), .MUX_FC3(cb_ex_1_mux_fc3), .MUX_SUB(cb_ex_1_mux_sub));
  Multiplexer #(.Bits(3)) multiplexer_4 (
    .sel(cb_ex_1_mux_fc3), .in_0(undriven_6), .in_1(3'b000), .out(multiplexer_4_out));
  Multiplexer #(.Bits(32)) multiplexer_5 (
    .sel(cb_ex_1_mux_alu), .in_0(undriven_8), .in_1(undriven_3), .out(multiplexer_5_out));
  Multiplexer #(.Selector_Bits(2)) multiplexer_6 (
    .sel(cb_ex_1_mux_sub), .in_0(1'b0), .in_1(undriven_5[5]), .in_2(1'b1), .in_3(1'b0),
    .out(multiplexer_6_out));
  UAL ual_1 (.sub(multiplexer_6_out), .funct3(multiplexer_4_out), .a(undriven_7), .b(multiplexer_5_out), .s(ual_1_s));
  BRANCH branch_1 (.fct3(undriven_6), .res(ual_1_s), .Taken(branch_1_taken));
  EX_REG ex_reg_1 ();
  CB_MEM cb_mem_1 (.OP_CODE(undriven_10), .MUX_MEM(cb_mem_1_mux_mem), .W_MEM(cb_mem_1_w_mem));
  RAMSinglePortSel #(.AddrBits(8), .Bits(32)) ramsingleportsel_2 (
    .A(undriven_11[9:2]), .CS(1'b1), .WE(cb_mem_1_w_mem), .OE(not_2_out), .D(ramsingleportsel_2_d));
  not not_2 (not_2_out, cb_mem_1_w_mem);
  assign ramsingleportsel_2_d = cb_mem_1_w_mem ? undriven_9 : 32'bz;  // Driver driver_1
  Multiplexer #(.Bits(32)) multiplexer_7 (
    .sel(cb_mem_1_mux_mem), .in_0(undriven_11), .in_1(ramsingleportsel_2_d), .out(multiplexer_7_out));
  MEM_REG mem_reg_1 ();
  Multiplexer #(.Bits(32)) multiplexer_8 (
    .sel(cb_callback_1_mux_res), .in_0(undriven_15), .in_1(undriven_16), .out(multiplexer_8_out));
  CB_CALLBACK cb_callback_1 (
    .OP_CODE(undriven_13), .TAKEN(undriven_14), .MUX_JUMP(cb_callback_1_mux_jump),
    .MUX_RES(cb_callback_1_mux_res), .MUX_PC(cb_callback_1_mux_pc), .MUX_JALR(cb_callback_1_mux_jalr),
    .W_REG(cb_callback_1_w_reg));
  Multiplexer #(.Bits(32)) multiplexer_9 (
    .sel(cb_callback_1_mux_jump), .in_0(undriven_12), .in_1(undriven_15), .out(multiplexer_9_out));
endmodule
