// Digital circuit DATA_PATH.dig as structural Verilog
module DATA_PATH (
  input  [1:0] MUX_IMM,
  input  CLK,
  input  WMEM,
  input  MuxMEM,
  input  MUX_PC,
  input  WPC,
  input  sub,
  input  Wreg,
  input  MUX_ALU,
  input  MUX_FC3,
  input  MUX_RES,
  input  MUX_JUMP
);

  wire branch_1_taken, not_1_out, not_2_out;
  wire [2:0] multiplexer_3_out, undriven_4;
  wire [4:0] undriven_2;
  wire [7:0] PC_q_2;
  wire [31:0] add_1_s, add_2_s, banc_de_registres_1_src1, banc_de_registres_1_src2, bitextender_1_out,
       bitextender_2_out, bitextender_3_out, bitextender_4_out, driver_1_out, multiplexer_1_out,
       multiplexer_2_out, multiplexer_4_out, multiplexer_5_out, multiplexer_6_out, multiplexer_7_out, PC_q,
       ramsingleportsel_1_d, ual_1_s, undriven_3, undriven_5, undriven_6, undriven_7, undriven_8, undriven_9,
       undriven_10, undriven_11;
  wire [31:7] undriven;

  Multiplexer #(.Bits(32)) multiplexer_1 (
    .sel(MUX_PC), .in_0(32'h4), .in_1(multiplexer_7_out), .out(multiplexer_1_out));
  Add #(.Bits(32)) add_1 (
    .a(multiplexer_1_out), .b({PC_q[31:10], PC_q_2, PC_q[1:0]}), .c_i(1'b0), .s(add_1_s));  // open: c_o
  D_FF #(.Bits(32)) PC (.D(add_1_s), .C(WPC), .Q({PC_q[31:10], PC_q_2, PC_q[1:0]}));  // open: nQ
  not not_1 (not_1_out, 1'b1);
  RAMSinglePortSel #(.AddrBits(8), .Bits(32)) ramsingleportsel_1 (
    .A(PC_q_2), .CS(1'b1), .WE(not_1_out), .OE(1'b1), .D(ramsingleportsel_1_d));
  Add #(.Bits(32)) add_2 (.a({PC_q[31:10], PC_q_2, PC_q[1:0]}), .b(32'h4), .c_i(1'b0), .s(add_2_s));  // open: c_o
  IF_REG if_reg_1 ();
  BitExtender #(.inputBits(12), .outputBits(32)) bitextender_1 (.in(undriven[31:20]), .out(bitextender_1_out));
  BitExtender #(.inputBits(12), .outputBits(32)) bitextender_2 (
    .in({undriven[31:25], undriven[11:7]}), .out(bitextender_2_out));
  Banc_De_Registres banc_de_registres_1 (
    .Wreg(Wreg), .rd(undriven_2), .rs1(undriven[19:15]), .rs2(undriven[24:20]), .res(multiplexer_6_out),
    .src1(banc_de_registres_1_src1), .src2(banc_de_registres_1_src2));  // open: x3
  BitExtender #(.inputBits(14), .outputBits(32)) bitextender_3 (
    .in({undriven[31], undriven[7], undriven[30:25], undriven[11:8], 2'b00}), .out(bitextender_3_out));
  BitExtender #(.inputBits(22), .outputBits(32)) bitextender_4 (
    .in({undriven[31], undriven[19:12], undriven[20], undriven[30:21], 2'b00}), .out(bitextender_4_out));
  Multiplexer #(.Selector_Bits(2), .Bits(32)) multiplexer_2 (
    .sel(MUX_IMM), .in_0(bitextender_1_out), .in_1(bitextender_2_out), .in_2(bitextender_3_out),
    .in_3(bitextender_4_out), .out(multiplexer_2_out));
  ID_REG id_reg_1 ();
  Multiplexer #(.Bits(3)) multiplexer_3 (.sel(MUX_FC3), .in_0(undriven_4), .in_1(3'b000), .out(multiplexer_3_out));
  Multiplexer #(.Bits(32)) multiplexer_4 (.sel(MUX_ALU), .in_0(undriven_6), .in_1(undriven_3), .out(multiplexer_4_out));
  UAL ual_1 (.sub(sub), .funct3(multiplexer_3_out), .a(undriven_5), .b(multiplexer_4_out), .s(ual_1_s));
  BRANCH branch_1 (.fct3(undriven_4), .res(ual_1_s), .Taken(branch_1_taken));
  EX_REG ex_reg_1 ();
  not not_2 (not_2_out, WMEM);
  assign driver_1_out = WMEM ? undriven_7 : 32'bz;  // Driver driver_1
  RAMSinglePortSel #(.AddrBits(8), .Bits(32)) ramsingleportsel_2 (
    .A(undriven_8[9:2]), .CS(1'b1), .WE(WMEM), .OE(not_2_out), .D(driver_1_out));
  Multiplexer #(.Bits(32)) multiplexer_5 (
    .sel(MuxMEM), .in_0(driver_1_out), .in_1(undriven_8), .out(multiplexer_5_out));
  MEM_REG mem_reg_1 ();
  Multiplexer #(.Bits(32)) multiplexer_6 (
    .sel(MUX_RES), .in_0(undriven_10), .in_1(undriven_11), .out(multiplexer_6_out));
  Multiplexer #(.Bits(32)) multiplexer_7 (
    .sel(MUX_JUMP), .in_0(undriven_9), .in_1(undriven_10), .out(multiplexer_7_out));
endmodule
