// Digital circuit ID_REG.dig as structural Verilog
module ID_REG (
  input  [31:0] SRC1,
  input  [31:0] PC_plus_4,
  input  W_ID,
  input  [31:0] SRC2,
  input  [31:0] IM,
  input  [4:0] RD,
  input  [6:0] OP_CODE,
  input  [2:0] FC3,
  input  [6:0] FC7,
  output [31:0] ID_PC_plus_4,
  output [31:0] ID_SRC1,
  output [31:0] ID_SRC2,
  output [31:0] ID_IM,
  output [4:0] ID_RD,
  output [6:0] ID_OP_CODE,
  output [2:0] ID_FC3,
  output [6:0] ID_FC7
);

  D_FF #(.Bits(32)) u_SRC1 (.D(SRC1), .C(W_ID), .Q(ID_SRC1));  // open: nQ
  D_FF #(.Bits(32)) u_SRC2 (.D(SRC2), .C(W_ID), .Q(ID_SRC2));  // open: nQ
  D_FF #(.Bits(32)) u_IM (.D(IM), .C(W_ID), .Q(ID_IM));  // open: nQ
  D_FF #(.Bits(5)) u_RD (.D(RD), .C(W_ID), .Q(ID_RD));  // open: nQ
  D_FF #(.Bits(3)) u_FC3 (.D(FC3), .C(W_ID), .Q(ID_FC3));  // open: nQ
  D_FF #(.Bits(7)) u_FC7 (.D(FC7), .C(W_ID), .Q(ID_FC7));  // open: nQ
  D_FF #(.Bits(7)) u_OP_CODE (.D(OP_CODE), .C(W_ID), .Q(ID_OP_CODE));  // open: nQ
  D_FF #(.Bits(32)) u_PC_plus_4 (.D(PC_plus_4), .C(W_ID), .Q(ID_PC_plus_4));  // open: nQ
endmodule
