// Digital circuit IF_REG.dig as structural Verilog
module IF_REG (
  input  [31:0] IR,
  input  [31:0] PC_plus_4,
  input  W_IF,
  output [31:0] IF_PC_plus_4,
  output [31:0] IF_IR
);

  D_FF #(.Bits(32)) u_IR (.D(IR), .C(W_IF), .Q(IF_IR));  // open: nQ
  D_FF #(.Bits(32)) u_PC_plus_4 (.D(PC_plus_4), .C(W_IF), .Q(IF_PC_plus_4));  // open: nQ
endmodule
