// Digital circuit UAL.dig as structural Verilog
module UAL (
  input  sub,
  input  [2:0] funct3,
  input  [31:0] a,
  input  [31:0] b,
  output [31:0] s
);

  wire [0:0] comparator_1_lt, comparator_2_lt;
  wire [31:0] ADD_SUB_s, and_1_out, barrelshifter_1_out, bitextender_1_out, or_1_out, SLL_out, xor_1_out,
       xor_2_out;

  BitExtender #(.inputBits(1), .outputBits(32)) bitextender_1 (.in(sub), .out(bitextender_1_out));
  assign xor_1_out = b ^ bitextender_1_out;  // XOr xor_1, 32 bits wide
  Add #(.Bits(32)) ADD_SUB (.a(a), .b(xor_1_out), .c_i(sub), .s(ADD_SUB_s));  // open: c_o
  BarrelShifter #(.Bits(32)) SLL (.in(a), .shift({1'b0, b[4:0]}), .out(SLL_out));
  Comparator #(.Signed("true"), .Bits(32)) comparator_1 (.a(a), .b(b), .lt(comparator_1_lt[0]));  // open: gt, eq
  Comparator #(.Bits(32)) comparator_2 (.a(a), .b(b), .lt(comparator_2_lt[0]));  // open: gt, eq
  assign xor_2_out = a ^ b;  // XOr xor_2, 32 bits wide
  BarrelShifter #(.Bits(32), .direction("right")) barrelshifter_1 (
    .in(a), .shift({1'b0, b[4:0]}), .out(barrelshifter_1_out));
  assign or_1_out = a | b;  // Or or_1, 32 bits wide
  assign and_1_out = a & b;  // And and_1, 32 bits wide
  Multiplexer #(.Selector_Bits(3), .Bits(32)) multiplexer_1 (
    .sel(funct3), .in_0(ADD_SUB_s), .in_1(SLL_out), .in_2({{31{1'b0}}, comparator_1_lt[0]}),
    .in_3({{31{1'b0}}, comparator_2_lt[0]}), .in_4(xor_2_out), .in_5(barrelshifter_1_out), .in_6(or_1_out),
    .in_7(and_1_out), .out(s));
endmodule
