// Digital circuit Mux 2_1.dig as structural Verilog
module Mux_2_1 (
  input  e0,
  input  e1,
  input  c,
  output out_1
);

  wire and_1_out, and_2_out, not_1_out;

  not not_1 (not_1_out, c);
  and and_1 (and_1_out, e0, not_1_out);
  and and_2 (and_2_out, e1, c);
  or or_1 (out_1, and_1_out, and_2_out);
endmodule
