// Digital circuit Add PG 8bit.dig as structural Verilog
module Add_PG_8bit (
  input  c0,
  input  a0,
  input  b0,
  input  a1,
  input  b1,
  input  a2,
  input  b2,
  input  a3,
  input  b3,
  input  a4,
  input  b4,
  input  a5,
  input  b5,
  input  a6,
  input  b6,
  input  a7,
  input  b7,
  output s0,
  output s1,
  output s2,
  output s3,
  output s4,
  output s5,
  output s6,
  output s7,
  output C7
);

  wire addpg_1bit_4_g, addpg_1bit_4_p, addpg_1bit_5_g, addpg_1bit_5_p, addpg_1bit_6_g, addpg_1bit_6_p,
       addpg_1bit_7_g, addpg_1bit_7_p, addpg_1bit_8_g, addpg_1bit_8_p, cc_8bit_1_p2, cc_8bit_1_p3,
       cc_8bit_1_p4, cc_8bit_1_p5, cc_8bit_1_p6, cc_8bit_1_p7, cc_8bit_1_p8, cc_8bit_1_p9, undriven,
       undriven_2, undriven_3, undriven_4, undriven_5;

  // CC_8bit cc_8bit_1: pin names not known; wires that end beside it: C7, cc_8bit_1_p2, cc_8bit_1_p3, cc_8bit_1_p4, cc_8bit_1_p5, cc_8bit_1_p6, cc_8bit_1_p7, cc_8bit_1_p8, cc_8bit_1_p9
  AddPG_1bit addpg_1bit_1 (.a(a7), .b(b7), .Cin(cc_8bit_1_p4), .s(s7), .G(cc_8bit_1_p3), .P(cc_8bit_1_p2));
  AddPG_1bit addpg_1bit_2 (.a(a6), .b(b6), .Cin(cc_8bit_1_p7), .s(s6), .G(cc_8bit_1_p6), .P(cc_8bit_1_p5));
  AddPG_1bit addpg_1bit_3 (.a(a5), .b(b5), .Cin(undriven), .s(s5), .G(cc_8bit_1_p9), .P(cc_8bit_1_p8));
  AddPG_1bit addpg_1bit_4 (.a(a4), .b(b4), .Cin(undriven_2), .s(s4), .G(addpg_1bit_4_g), .P(addpg_1bit_4_p));
  AddPG_1bit addpg_1bit_5 (.a(a3), .b(b3), .Cin(undriven_3), .s(s3), .G(addpg_1bit_5_g), .P(addpg_1bit_5_p));
  AddPG_1bit addpg_1bit_6 (.a(a2), .b(b2), .Cin(undriven_4), .s(s2), .G(addpg_1bit_6_g), .P(addpg_1bit_6_p));
  AddPG_1bit addpg_1bit_7 (.a(a1), .b(b1), .Cin(undriven_5), .s(s1), .G(addpg_1bit_7_g), .P(addpg_1bit_7_p));
  AddPG_1bit addpg_1bit_8 (.a(a0), .b(b0), .Cin(c0), .s(s0), .G(addpg_1bit_8_g), .P(addpg_1bit_8_p));
endmodule
