// Digital circuit CC 8bit.dig as structural Verilog
module CC_8bit (
  input  C0,
  input  P0,
  input  G0,
  input  P1,
  input  G1,
  input  P2,
  input  G2,
  input  P3,
  input  G3,
  input  P4,
  input  G4,
  input  P5,
  input  G5,
  input  P6,
  input  G6,
  input  P7,
  input  G7,
  output Cout0,
  output Cout1,
  output Cout2,
  output Cout3,
  output Cout4,
  output Cout5,
  output Cout6,
  output Cout7
);

  CC_1bit cc_1bit_1 (.G(G7), .P(P7), .Cin(Cout6), .Cout(Cout7));
  CC_1bit cc_1bit_2 (.G(G6), .P(P6), .Cin(Cout5), .Cout(Cout6));
  CC_1bit cc_1bit_3 (.G(G5), .P(P5), .Cin(Cout4), .Cout(Cout5));
  CC_1bit cc_1bit_4 (.G(G4), .P(P4), .Cin(Cout3), .Cout(Cout4));
  CC_1bit cc_1bit_5 (.G(G3), .P(P3), .Cin(Cout2), .Cout(Cout3));
  CC_1bit cc_1bit_6 (.G(G2), .P(P2), .Cin(Cout1), .Cout(Cout2));
  CC_1bit cc_1bit_7 (.G(G1), .P(P1), .Cin(Cout0), .Cout(Cout1));
  CC_1bit cc_1bit_8 (.G(G0), .P(P0), .Cin(C0), .Cout(Cout0));
endmodule
