// Digital circuit Registre_8Bit.dig as structural Verilog
module Registre_8Bit (
  input  e7,
  input  e6,
  input  e5,
  input  e4,
  input  e3,
  input  e2,
  input  e1,
  input  e0,
  input  W,
  output s7,
  output s6,
  output s5,
  output s4,
  output s3,
  output s2,
  output s1,
  output s0
);

  D_FF d_ff_1 (.D(e7), .C(W), .Q(s7));  // open: nQ
  D_FF d_ff_2 (.D(e6), .C(W), .Q(s6));  // open: nQ
  D_FF d_ff_3 (.D(e5), .C(W), .Q(s5));  // open: nQ
  D_FF d_ff_4 (.D(e4), .C(W), .Q(s4));  // open: nQ
  D_FF d_ff_5 (.D(e3), .C(W), .Q(s3));  // open: nQ
  D_FF d_ff_6 (.D(e2), .C(W), .Q(s2));  // open: nQ
  D_FF d_ff_7 (.D(e1), .C(W), .Q(s1));  // open: nQ
  D_FF d_ff_8 (.D(e0), .C(W), .Q(s0));  // open: nQ
endmodule
