// Digital circuit Compteur_a_saturation.dig as structural Verilog
module Compteur_a_saturation (
  input  W,
  input  inc,
  output s0,
  output s1,
  output s2
);

  wire and_1_out, and_2_out, and_3_out, and_4_out, and_5_out, and_6_out, and_7_out, and_8_out, and_9_out,
       and_10_out, D0_nq, D1_nq, multiplexer_1_out, multiplexer_2_out, multiplexer_3_out, not_1_out,
       not_2_out, or_1_out, or_2_out, or_3_out, or_4_out, or_5_out, or_6_out, xor_1_out;

  and and_1 (and_1_out, s0, s1);
  or or_1 (or_1_out, and_1_out, s2);
  and and_2 (and_2_out, or_2_out, s2);
  or or_2 (or_2_out, s0, s1);
  Multiplexer multiplexer_1 (.sel(inc), .in_0(and_2_out), .in_1(or_1_out), .out(multiplexer_1_out));
  D_FF D2 (.D(multiplexer_1_out), .C(W), .Q(s2));  // open: nQ
  and and_3 (and_3_out, s1, s2);
  or or_3 (or_3_out, xor_1_out, and_3_out);
  or or_4 (or_4_out, and_7_out, and_4_out);
  xor xor_1 (xor_1_out, s1, s0);
  Multiplexer multiplexer_2 (.sel(inc), .in_0(or_4_out), .in_1(or_3_out), .out(multiplexer_2_out));
  and and_4 (and_4_out, s2, and_6_out);
  and and_5 (and_5_out, s1, s2);
  and and_6 (and_6_out, not_2_out, not_1_out);
  D_FF D1 (.D(multiplexer_2_out), .C(W), .Q(s1), .nQ(D1_nq));
  not not_1 (not_1_out, s1);
  not not_2 (not_2_out, s0);
  and and_7 (and_7_out, s1, s0);
  and and_8 (and_8_out, s2, D1_nq);
  and and_9 (and_9_out, D0_nq, 1'b1);
  or or_5 (or_5_out, s1, and_8_out);
  or or_6 (or_6_out, and_5_out, and_9_out);
  and and_10 (and_10_out, D0_nq, or_5_out);
  Multiplexer multiplexer_3 (.sel(inc), .in_0(and_10_out), .in_1(or_6_out), .out(multiplexer_3_out));
  D_FF D0 (.D(multiplexer_3_out), .C(W), .Q(s0), .nQ(D0_nq));
endmodule
