// Digital circuit compteur_decompteur_modulo8.dig as structural Verilog
module compteur_decompteur_modulo8 (
  input  inc,
  input  raz,
  input  clk,
  output s0,
  output s1,
  output s2
);

  wire and_1_out, and_2_out, and_3_out, and_4_out, and_5_out, and_6_out, and_7_out, and_8_out, and_9_out,
       and_10_out, and_11_out, and_12_out, and_13_out, and_14_out, and_15_out, and_16_out, and_17_out,
       and_18_out, and_19_out, and_20_out, and_21_out, and_22_out, and_23_out, D0_nq, D1_nq, D2_nq,
       not_1_out, not_2_out, or_1_out, or_2_out, or_3_out, or_4_out, or_5_out, or_6_out, or_7_out, or_8_out;

  not not_1 (not_1_out, raz);
  not not_2 (not_2_out, inc);
  and and_1 (and_1_out, or_1_out, not_1_out);
  D_FF D2 (.D(and_1_out), .C(clk), .Q(s2), .nQ(D2_nq));
  or or_1 (or_1_out, and_3_out, and_2_out);
  and and_2 (and_2_out, D2_nq, or_5_out);
  and and_3 (and_3_out, s2, or_2_out);
  or or_2 (or_2_out, or_3_out, and_16_out);
  or or_3 (or_3_out, and_18_out, and_17_out);
  or or_4 (or_4_out, or_6_out, and_7_out);
  and and_4 (and_4_out, or_4_out, not_1_out);
  or or_5 (or_5_out, and_9_out, and_8_out);
  or or_6 (or_6_out, and_6_out, and_5_out);
  and and_5 (and_5_out, or_7_out, s0);
  and and_6 (and_6_out, D1_nq, or_8_out);
  and and_7 (and_7_out, inc, and_10_out);
  or or_7 (or_7_out, and_11_out, and_14_out);
  and and_8 (and_8_out, and_12_out, s0);
  and and_9 (and_9_out, and_13_out, D0_nq);
  and and_10 (and_10_out, s1, D0_nq);
  and and_11 (and_11_out, and_15_out, not_2_out);
  or or_8 (or_8_out, and_21_out, and_20_out);
  D_FF D1 (.D(and_4_out), .C(clk), .Q(s1), .nQ(D1_nq));
  and and_12 (and_12_out, inc, s1);
  and and_13 (and_13_out, not_2_out, D1_nq);
  and and_14 (and_14_out, inc, and_19_out);
  and and_15 (and_15_out, D2_nq, s1);
  and and_16 (and_16_out, D0_nq, s1);
  and and_17 (and_17_out, s0, not_2_out);
  and and_18 (and_18_out, D1_nq, inc);
  and and_19 (and_19_out, s2, D1_nq);
  and and_20 (and_20_out, inc, and_23_out);
  and and_21 (and_21_out, not_2_out, D0_nq);
  and and_22 (and_22_out, D0_nq, not_1_out);
  and and_23 (and_23_out, D2_nq, s0);
  D_FF D0 (.D(and_22_out), .C(clk), .Q(s0), .nQ(D0_nq));
endmodule
