// Digital circuit compteur_modulo8.dig as structural Verilog
module compteur_modulo8 (
  input  raz,
  input  W,
  output s0,
  output s1,
  output s2
);

  wire and_1_out, and_2_out, and_3_out, and_4_out, and_5_out, and_6_out, D0_nq, not_1_out, or_1_out,
       xor_1_out, xor_2_out;

  not not_1 (not_1_out, raz);
  and and_1 (and_1_out, D0_nq, not_1_out);
  and and_2 (and_2_out, s0, not_1_out);
  xor xor_1 (xor_1_out, s2, s1);
  and and_3 (and_3_out, and_1_out, s2);
  and and_4 (and_4_out, and_2_out, xor_1_out);
  or or_1 (or_1_out, and_3_out, and_4_out);
  D_FF D2 (.D(or_1_out), .C(W), .Q(s2));  // open: nQ
  xor xor_2 (xor_2_out, s0, s1);
  and and_5 (and_5_out, xor_2_out, not_1_out);
  D_FF D1 (.D(and_5_out), .C(W), .Q(s1));  // open: nQ
  and and_6 (and_6_out, D0_nq, not_1_out);
  D_FF D0 (.D(and_6_out), .C(W), .Q(s0), .nQ(D0_nq));
endmodule
