// Digital circuit Add 8bit.dig as structural Verilog
module Add_8bit (
  input  a0,
  input  b0,
  input  a1,
  input  b1,
  input  a2,
  input  b2,
  input  a3,
  input  b3,
  input  a4,
  input  b4,
  input  a5,
  input  b5,
  input  a6,
  input  b6,
  input  a7,
  input  b7,
  input  Cin,
  output S7,
  output Cout,
  output S6,
  output S5,
  output S4,
  output S3,
  output S2,
  output S1,
  output S0
);

  wire add_1bit_2_cout, add_1bit_3_cout, add_1bit_4_cout, add_1bit_5_cout, add_1bit_6_cout, add_1bit_7_cout,
       add_1bit_8_cout;

  Add_1bit add_1bit_1 (.a(b7), .b(a7), .cin(add_1bit_2_cout), .S(S7), .Cout(Cout));
  Add_1bit add_1bit_2 (.a(b6), .b(a6), .cin(add_1bit_3_cout), .S(S6), .Cout(add_1bit_2_cout));
  Add_1bit add_1bit_3 (.a(b5), .b(a5), .cin(add_1bit_4_cout), .S(S5), .Cout(add_1bit_3_cout));
  Add_1bit add_1bit_4 (.a(b4), .b(a4), .cin(add_1bit_5_cout), .S(S4), .Cout(add_1bit_4_cout));
  Add_1bit add_1bit_5 (.a(b3), .b(a3), .cin(add_1bit_6_cout), .S(S3), .Cout(add_1bit_5_cout));
  Add_1bit add_1bit_6 (.a(b2), .b(a2), .cin(add_1bit_7_cout), .S(S2), .Cout(add_1bit_6_cout));
  Add_1bit add_1bit_7 (.a(b1), .b(a1), .cin(add_1bit_8_cout), .S(S1), .Cout(add_1bit_7_cout));
  Add_1bit add_1bit_8 (.a(b0), .b(a0), .cin(Cin), .S(S0), .Cout(add_1bit_8_cout));
endmodule
