// Digital circuit Circuit_De_Controle.dig as structural Verilog
module Circuit_De_Controle (
  input  B0,
  input  Fin,
  input  Clk,
  output Raz,
  output Wop,
  output Wres,
  output Dec
);

  wire and_1_out, and_2_out, and_3_out, and_6_out, and_7_out, and_9_out, and_11_out, and_12_out, and_13_out,
       D0_nq, D0_q, D1_nq, D1_q, not_1_out, or_1_out, or_2_out, or_3_out, or_4_out;

  D_FF D1 (.D(or_2_out), .C(Clk), .Q(D1_q), .nQ(D1_nq));
  and and_1 (and_1_out, D0_nq, or_1_out);
  or or_1 (or_1_out, not_1_out, and_2_out);
  or or_2 (or_2_out, and_1_out, and_6_out);
  and and_2 (and_2_out, Fin, D1_q);
  and and_3 (and_3_out, D0_nq, D1_nq);
  and and_4 (Raz, and_3_out, Clk);
  and and_5 (Wop, D0_nq, Clk);
  and and_6 (and_6_out, D1_nq, or_3_out);
  or or_3 (or_3_out, not_1_out, D0_q);
  not not_1 (not_1_out, B0);
  and and_7 (and_7_out, D0_q, D1_nq);
  and and_8 (Wres, and_7_out, Clk);
  and and_9 (and_9_out, D0_nq, D1_q);
  and and_10 (Dec, and_9_out, Clk);
  D_FF D0 (.D(and_12_out), .C(Clk), .Q(D0_q), .nQ(D0_nq));
  and and_11 (and_11_out, B0, 1'b1);
  or or_4 (or_4_out, and_11_out, and_13_out);
  and and_12 (and_12_out, or_4_out, D0_nq);
  and and_13 (and_13_out, D1_q, Fin);
endmodule
