// Digital circuit Multiplieur_Sequentielle.dig as structural Verilog
module Multiplieur_Sequentielle (
  input  a0,
  input  a1,
  input  a2,
  input  a3,
  input  b0,
  input  b1,
  input  b2,
  input  b3,
  input  clk,
  output Cout,
  output s0,
  output s1,
  output s2,
  output s3,
  output s4,
  output s5,
  output s6,
  output s7,
  output fin
);

  wire add_8bit_1_s0, add_8bit_1_s1, add_8bit_1_s2, add_8bit_1_s3, add_8bit_1_s4, add_8bit_1_s5,
       add_8bit_1_s6, add_8bit_1_s7, B_s0, circuit_de_controle_1_dec, circuit_de_controle_1_raz,
       circuit_de_controle_1_wop, circuit_de_controle_1_wres, compteur_4bit_1_s0, compteur_4bit_1_s1,
       not_1_out, not_2_out, registre_decalage_droite_gauche_4bit_1_s0,
       registre_decalage_droite_gauche_4bit_1_s1, registre_decalage_droite_gauche_4bit_1_s2,
       registre_decalage_droite_gauche_4bit_1_s3;

  Registre_decalage_droite_gauche_4bit registre_decalage_droite_gauche_4bit_1 (
    .W(circuit_de_controle_1_wop), .left(circuit_de_controle_1_dec), .dec(circuit_de_controle_1_dec),
    .e3(a3), .e2(a2), .e1(a1), .e0(a0), .s3(registre_decalage_droite_gauche_4bit_1_s3),
    .s2(registre_decalage_droite_gauche_4bit_1_s2), .s1(registre_decalage_droite_gauche_4bit_1_s1),
    .s0(registre_decalage_droite_gauche_4bit_1_s0));
  Add_8bit add_8bit_1 (
    .a0(registre_decalage_droite_gauche_4bit_1_s0), .b0(s0), .a1(registre_decalage_droite_gauche_4bit_1_s1),
    .b1(s1), .a2(registre_decalage_droite_gauche_4bit_1_s2), .b2(s2),
    .a3(registre_decalage_droite_gauche_4bit_1_s3), .b3(s3), .a4(1'b0), .b4(s4), .a5(1'b0), .b5(s5),
    .a6(1'b0), .b6(s6), .a7(1'b0), .b7(s7), .Cin(1'b0), .S7(add_8bit_1_s7), .Cout(Cout), .S6(add_8bit_1_s6),
    .S5(add_8bit_1_s5), .S4(add_8bit_1_s4), .S3(add_8bit_1_s3), .S2(add_8bit_1_s2), .S1(add_8bit_1_s1),
    .S0(add_8bit_1_s0));
  Registre_8Bit registre_8bit_1 (
    .e7(add_8bit_1_s7), .e6(add_8bit_1_s6), .e5(add_8bit_1_s5), .e4(add_8bit_1_s4), .e3(add_8bit_1_s3),
    .e2(add_8bit_1_s2), .e1(add_8bit_1_s1), .e0(add_8bit_1_s0), .W(circuit_de_controle_1_wres),
    .reset(circuit_de_controle_1_raz), .s7(s7), .s6(s6), .s5(s5), .s4(s4), .s3(s3), .s2(s2), .s1(s1), .s0(s0));
  Compteur_4bit compteur_4bit_1 (.clk(clk), .s0(compteur_4bit_1_s0), .s1(compteur_4bit_1_s1));
  and and_1 (fin, not_1_out, not_2_out);
  not not_1 (not_1_out, compteur_4bit_1_s0);
  not not_2 (not_2_out, compteur_4bit_1_s1);
  Circuit_De_Controle circuit_de_controle_1 (
    .B0(B_s0), .Fin(fin), .Clk(clk), .Raz(circuit_de_controle_1_raz), .Wop(circuit_de_controle_1_wop),
    .Wres(circuit_de_controle_1_wres), .Dec(circuit_de_controle_1_dec));
  Registre_decalage_droite_gauche_4bit B (
    .W(circuit_de_controle_1_wop), .left(1'b0), .dec(circuit_de_controle_1_dec), .e3(b3), .e2(b2), .e1(b1),
    .e0(b0), .s0(B_s0));  // open: s3, s2, s1
endmodule
