// Digital circuit Data_Path_1.1.dig as structural Verilog
module Data_Path_1_1 (
  input  W_IR,
  input  W_PC,
  input  G_PC,
  input  W_RES,
  input  SUB,
  input  MUX_ALU,
  input  G_ALU,
  input  W_MAR,
  input  W_MDR,
  input  MUX_MDR,
  input  G_MDR,
  input  W_MDR_2
);

  wire not_1_out;
  wire [2:0] IR_q_2;
  wire [7:0] MAR_q_2;
  wire [31:0] add_1_s, banc_de_registres_1_src1, banc_de_registres_1_src2, bitextender_1_out, driver_1_out,
       IR_q, MAR_q, MDR_q, multiplexer_1_out, multiplexer_2_out, PC_q, ramsingleportsel_1_d, ual_1_s;

  Register #(.Bits(32)) PC (.D(add_1_s), .C(W_PC), .en(W_PC), .Q(PC_q));
  Add #(.Bits(32)) add_1 (.a(32'h4), .b(PC_q), .c_i(1'b0), .s(add_1_s));  // open: c_o
  Register #(.Bits(32)) IR (.D(driver_1_out), .C(W_IR), .en(W_IR), .Q({IR_q[31:15], IR_q_2, IR_q[11:0]}));
  assign driver_1_out = G_PC ? PC_q : 32'bz;  // Driver driver_1
  BitExtender #(.inputBits(12), .outputBits(32)) bitextender_1 (.in(IR_q[31:20]), .out(bitextender_1_out));
  Register #(.Bits(32)) MAR (.D(driver_1_out), .C(W_MAR), .en(W_MAR), .Q({MAR_q[31:10], MAR_q_2, MAR_q[1:0]}));
  Banc_De_Registres banc_de_registres_1 (
    .clk(W_RES), .rd(IR_q[11:7]), .rs1(IR_q[19:15]), .rs2(IR_q[24:20]), .res(driver_1_out),
    .src1(banc_de_registres_1_src1), .src2(banc_de_registres_1_src2));
  not not_1 (not_1_out, W_MDR_2);
  RAMSinglePortSel #(.AddrBits(8), .Bits(32)) ramsingleportsel_1 (
    .A(MAR_q_2), .CS(1'b1), .WE(W_MDR_2), .OE(not_1_out), .D(ramsingleportsel_1_d));
  Multiplexer #(.Bits(32)) multiplexer_1 (
    .sel(MUX_ALU), .in_0(banc_de_registres_1_src2), .in_1(bitextender_1_out), .out(multiplexer_1_out));
  Multiplexer #(.Bits(32)) multiplexer_2 (
    .sel(MUX_MDR), .in_0(ramsingleportsel_1_d), .in_1(driver_1_out), .out(multiplexer_2_out));
  Register #(.Bits(32)) MDR (.D(multiplexer_2_out), .C(W_MDR), .en(W_MDR), .Q(MDR_q));
  UAL ual_1 (.sub(SUB), .funct3(IR_q_2), .a(banc_de_registres_1_src1), .b(multiplexer_1_out), .s(ual_1_s));
  assign driver_1_out = G_MDR ? MDR_q : 32'bz;  // Driver driver_2
  assign ramsingleportsel_1_d = W_MDR_2 ? MDR_q : 32'bz;  // Driver driver_3
  assign driver_1_out = G_ALU ? ual_1_s : 32'bz;  // Driver driver_4
endmodule
