// Digital circuit UAL.dig as structural Verilog
module UAL (
  input  sub,
  input  [2:0] funct3,
  input  b0,
  input  b1,
  input  b2,
  input  b3,
  input  b4,
  input  b5,
  input  b6,
  input  b7,
  input  b8,
  input  b9,
  input  b10,
  input  b11,
  input  b12,
  input  b13,
  input  b14,
  input  b15,
  input  b16,
  input  b17,
  input  b18,
  input  b19,
  input  b20,
  input  b21,
  input  b22,
  input  b23,
  input  b24,
  input  b25,
  input  b26,
  input  b27,
  input  b28,
  input  b29,
  input  b30,
  input  b31,
  input  a0,
  input  a1,
  input  a2,
  input  a3,
  input  a4,
  input  a5,
  input  a6,
  input  a7,
  input  a8,
  input  a9,
  input  a10,
  input  a11,
  input  a12,
  input  a13,
  input  a14,
  input  a15,
  input  a16,
  input  a17,
  input  a18,
  input  a19,
  input  a20,
  input  a21,
  input  a22,
  input  a23,
  input  a24,
  input  a25,
  input  a26,
  input  a27,
  input  a28,
  input  a29,
  input  a30,
  input  a31,
  output [31:0] s
);

  wire [0:0] comparator_1_lt, comparator_2_lt;
  wire [31:0] ADD_SUB_s, and_1_out, barrelshifter_1_out, or_1_out, SLL_out, xor_1_out, xor_2_out;

  assign xor_1_out = {b31, b30, b29, b28, b27, b26, b25, b24, b23, b22, b21, b20, b19, b18, b17, b16, b15, b14, b13, b12, b11, b10, b9, b8, b7, b6, b5, b4, b3, b2, b1, b0} ^ {32{sub}};  // XOr xor_1, 32 bits wide
  Add #(.Bits(32)) ADD_SUB (
    .a({a31, a30, a29, a28, a27, a26, a25, a24, a23, a22, a21, a20, a19, a18, a17, a16, a15, a14, a13, a12, a11, a10, a9, a8, a7, a6, a5, a4, a3, a2, a1, a0}),
    .b(xor_1_out), .c_i(sub), .s(ADD_SUB_s));  // open: c_o
  BarrelShifter #(.Bits(32)) SLL (
    .in({a31, a30, a29, a28, a27, a26, a25, a24, a23, a22, a21, a20, a19, a18, a17, a16, a15, a14, a13, a12, a11, a10, a9, a8, a7, a6, a5, a4, a3, a2, a1, a0}),
    .shift({b5, b4, b3, b2, b1, b0}), .out(SLL_out));
  Comparator #(.Bits(32), .Signed("true")) comparator_1 (
    .a({a31, a30, a29, a28, a27, a26, a25, a24, a23, a22, a21, a20, a19, a18, a17, a16, a15, a14, a13, a12, a11, a10, a9, a8, a7, a6, a5, a4, a3, a2, a1, a0}),
    .b({b31, b30, b29, b28, b27, b26, b25, b24, b23, b22, b21, b20, b19, b18, b17, b16, b15, b14, b13, b12, b11, b10, b9, b8, b7, b6, b5, b4, b3, b2, b1, b0}),
    .lt(comparator_1_lt[0]));  // open: gt, eq
  Comparator #(.Bits(32)) comparator_2 (
    .a({a31, a30, a29, a28, a27, a26, a25, a24, a23, a22, a21, a20, a19, a18, a17, a16, a15, a14, a13, a12, a11, a10, a9, a8, a7, a6, a5, a4, a3, a2, a1, a0}),
    .b({b31, b30, b29, b28, b27, b26, b25, b24, b23, b22, b21, b20, b19, b18, b17, b16, b15, b14, b13, b12, b11, b10, b9, b8, b7, b6, b5, b4, b3, b2, b1, b0}),
    .lt(comparator_2_lt[0]));  // open: gt, eq
  assign xor_2_out = {a31, a30, a29, a28, a27, a26, a25, a24, a23, a22, a21, a20, a19, a18, a17, a16, a15, a14, a13, a12, a11, a10, a9, a8, a7, a6, a5, a4, a3, a2, a1, a0} ^ {b31, b30, b29, b28, b27, b26, b25, b24, b23, b22, b21, b20, b19, b18, b17, b16, b15, b14, b13, b12, b11, b10, b9, b8, b7, b6, b5, b4, b3, b2, b1, b0};  // XOr xor_2, 32 bits wide
  BarrelShifter #(.Bits(32)) barrelshifter_1 (
    .in({a31, a30, a29, a28, a27, a26, a25, a24, a23, a22, a21, a20, a19, a18, a17, a16, a15, a14, a13, a12, a11, a10, a9, a8, a7, a6, a5, a4, a3, a2, a1, a0}),
    .shift({b5, b4, b3, b2, b1, b0}), .out(barrelshifter_1_out));
  assign or_1_out = {a31, a30, a29, a28, a27, a26, a25, a24, a23, a22, a21, a20, a19, a18, a17, a16, a15, a14, a13, a12, a11, a10, a9, a8, a7, a6, a5, a4, a3, a2, a1, a0} | {b31, b30, b29, b28, b27, b26, b25, b24, b23, b22, b21, b20, b19, b18, b17, b16, b15, b14, b13, b12, b11, b10, b9, b8, b7, b6, b5, b4, b3, b2, b1, b0};  // Or or_1, 32 bits wide
  assign and_1_out = {a31, a30, a29, a28, a27, a26, a25, a24, a23, a22, a21, a20, a19, a18, a17, a16, a15, a14, a13, a12, a11, a10, a9, a8, a7, a6, a5, a4, a3, a2, a1, a0} & {b31, b30, b29, b28, b27, b26, b25, b24, b23, b22, b21, b20, b19, b18, b17, b16, b15, b14, b13, b12, b11, b10, b9, b8, b7, b6, b5, b4, b3, b2, b1, b0};  // And and_1, 32 bits wide
  Multiplexer #(.Selector_Bits(3), .Bits(32)) multiplexer_1 (
    .sel(funct3), .in_0(ADD_SUB_s), .in_1(SLL_out), .in_2({{31{1'b0}}, comparator_1_lt[0]}),
    .in_3({{31{1'b0}}, comparator_2_lt[0]}), .in_4(xor_2_out), .in_5(barrelshifter_1_out), .in_6(or_1_out),
    .in_7(and_1_out), .out(s));
endmodule
